// Logisim project Universalgateshiffters.circ as structural Verilog: 1 circuit, main circuit main
module main (
  input  in_1,
  input  in_2,
  input  [1:0] in_3,
  input  in_4,
  input  in_5,
  input  in_6,
  input  in_7,
  input  in_8,
  input  in_9
);

  wire clock_1_out, d_ff_1_q, d_ff_2_q, d_ff_3_q, d_ff_4_q, multiplexer_1_out, multiplexer_2_out,
       multiplexer_3_out, multiplexer_4_out;

  Clock clock_1 (.out(clock_1_out));
  D_Flip_Flop #(.trigger("falling")) d_ff_1 (
    .D(multiplexer_1_out), .clk(clock_1_out), .Q(d_ff_1_q), .preset(in_1), .reset(in_2));  // open: Qn
  Multiplexer #(.select(2)) multiplexer_1 (
    .in0(d_ff_1_q), .in1(in_4), .in2(d_ff_2_q), .in3(in_5), .out(multiplexer_1_out), .sel(in_3));
  D_Flip_Flop #(.trigger("falling")) d_ff_2 (
    .D(multiplexer_2_out), .clk(clock_1_out), .Q(d_ff_2_q), .preset(in_1), .reset(in_2));  // open: Qn
  Multiplexer #(.select(2)) multiplexer_2 (
    .in0(d_ff_2_q), .in1(d_ff_1_q), .in2(d_ff_3_q), .in3(in_7), .out(multiplexer_2_out), .sel(in_3));
  D_Flip_Flop #(.trigger("falling")) d_ff_3 (
    .D(multiplexer_3_out), .clk(clock_1_out), .Q(d_ff_3_q), .preset(in_1), .reset(in_2));  // open: Qn
  Multiplexer #(.select(2)) multiplexer_3 (
    .in0(d_ff_3_q), .in1(d_ff_2_q), .in2(d_ff_4_q), .in3(in_8), .out(multiplexer_3_out), .sel(in_3));
  D_Flip_Flop #(.trigger("falling")) d_ff_4 (
    .D(multiplexer_4_out), .clk(clock_1_out), .Q(d_ff_4_q), .preset(in_1), .reset(in_2));  // open: Qn
  Multiplexer #(.select(2)) multiplexer_4 (
    .in0(d_ff_4_q), .in1(d_ff_3_q), .in2(in_6), .in3(in_9), .out(multiplexer_4_out), .sel(in_3));
  LED led_1 (.in(d_ff_1_q));
  LED led_2 (.in(d_ff_2_q));
  LED led_3 (.in(d_ff_3_q));
  LED led_4 (.in(d_ff_4_q));
endmodule
